// Logisim project mips.circ as structural Verilog: 4 circuits, main circuit main
module main (
);

  wire and_1_out, and_2_out, BEQ, BNE, CLK, EQUAL, JUMP, MEM_WR, MUX_DIN, REGDEST, ULAOPSRC, ULASRC, WR;
  wire [0:0] or_1_out;
  wire [2:0] ULAOP;
  wire [4:0] multiplexer_1_out;
  wire [5:0] bit_extender_1_out, FUNCT, multiplexer_4_out;
  wire [15:6] IMMEDIATE;
  wire [27:0] PC;
  wire [31:0] banco_registradores_1_r1, BEQ_BNE_ADDRS, bit_extender_2_out, BR_RT, DIN, IMM_EXT, MEM_OUT,
       multiplexer_2_out, multiplexer_3_out, PC_4, ULA_OUT;
  wire [31:16] INSTRUCTION;
  wire [31:28] JUMP_ADDRS;

  Adder #(.width(32)) adder_1 (.a({JUMP_ADDRS, PC}), .b(32'h4), .out(PC_4));  // open: cin, cout
  Multiplexer #(.width(5), .enable("false")) multiplexer_1 (
    .in0(IMMEDIATE[15:11]), .in1(INSTRUCTION[20:16]), .out(multiplexer_1_out), .sel(REGDEST));
  Multiplexer #(.select(2), .width(32), .enable("false")) multiplexer_2 (
    .in0(PC_4), .in1(BEQ_BNE_ADDRS), .in2({JUMP_ADDRS, INSTRUCTION[25:16], IMMEDIATE, FUNCT, 2'b00}),
    .out(multiplexer_2_out), .sel({JUMP, or_1_out[0]}));  // open: in3
  Register #(.width(32)) register_1 (.D(multiplexer_2_out), .Q({JUMP_ADDRS, PC}), .clk(CLK));  // open: en, clr
  and and_1 (and_1_out, EQUAL, BEQ);
  or or_1 (or_1_out[0], and_1_out, and_2_out);
  and and_2 (and_2_out, ~EQUAL, BNE);  // AND_Gate
  banco_registradores banco_registradores_1 (
    .R1_num(INSTRUCTION[25:21]), .R2_num(INSTRUCTION[20:16]), .RW(multiplexer_1_out), .Din(DIN), .WE(WR),
    .clk(CLK), .R1(banco_registradores_1_r1), .R2(BR_RT));  // open: a0, v0
  Clock clock_1 (.out(CLK));
  RAM #(.addrWidth(16), .dataWidth(32)) ram_1 (
    .addr(PC[17:2]), .data({INSTRUCTION, IMMEDIATE, FUNCT}), .clk(CLK));  // open: sel, ld, clr
  assign bit_extender_1_out = {{3{1'b0}}, ULAOP};  // Bit_Extender bit_extender_1
  ULA ula_1 (
    .A(banco_registradores_1_r1), .B(multiplexer_3_out), .Resultado(ULA_OUT), .OP(multiplexer_4_out),
    .igual(EQUAL));
  Multiplexer #(.width(32), .enable("false")) multiplexer_3 (
    .in0(BR_RT), .in1(IMM_EXT), .out(multiplexer_3_out), .sel(ULASRC));
  Multiplexer #(.width(6), .enable("false")) multiplexer_4 (
    .in0(FUNCT), .in1(bit_extender_1_out), .out(multiplexer_4_out), .sel(ULAOPSRC));
  UC UC (
    .UC5(INSTRUCTION[31]), .UC4(INSTRUCTION[30]), .UC3(INSTRUCTION[29]), .UC2(INSTRUCTION[28]),
    .UC1(INSTRUCTION[27]), .WR(WR), .UC0(INSTRUCTION[26]), .BEQ(BEQ), .BNE(BNE), .ULASRC(ULASRC),
    .REGDEST(REGDEST), .JUMP(JUMP), .ULAOP02(ULAOP[2]), .ULAOP01(ULAOP[1]), .ULAOP00(ULAOP[0]),
    .ULAOPSRC(ULAOPSRC), .MUX_DIN(MUX_DIN), .MEM_WR(MEM_WR));
  Multiplexer #(.width(32), .enable("false")) multiplexer_5 (.in0(ULA_OUT), .in1(MEM_OUT), .out(DIN), .sel(MUX_DIN));
  assign bit_extender_2_out = {{14{IMMEDIATE[15]}}, {IMMEDIATE, FUNCT, 2'b00}};  // Bit_Extender bit_extender_2
  Adder #(.width(32)) adder_2 (.a(bit_extender_2_out), .b(PC_4), .out(BEQ_BNE_ADDRS));  // open: cin, cout
  assign IMM_EXT = {{16{IMMEDIATE[15]}}, {IMMEDIATE, FUNCT}};  // Bit_Extender bit_extender_3
  RAM #(.addrWidth(16), .dataWidth(32), .bus("separate")) ram_2 (
    .addr(ULA_OUT[17:2]), .din(BR_RT), .data(MEM_OUT), .str(MEM_WR), .clk(CLK));  // open: sel, ld, clr

  // Other names for the same wires on the sheet: IMMEDIATE[5:0] = FUNCT; INSTRUCTION[15:0] = {IMMEDIATE, FUNCT};
  //   JUMP_ADDRS[27:2] = {INSTRUCTION[25:16], IMMEDIATE, FUNCT};
  //   LABELJ[25:0] = {INSTRUCTION[25:16], IMMEDIATE, FUNCT}; SHAMT[4:0] = IMMEDIATE[10:6]; RD[4:0] = IMMEDIATE[15:11];
  //   OPCODE[5:0] = INSTRUCTION[31:26]; RT[4:0] = INSTRUCTION[20:16]; RS[4:0] = INSTRUCTION[25:21];
  //   MEM_IN[31:0] = BR_RT; PC_UPPER16[15:0] = {JUMP_ADDRS, PC[27:16]}; PC[31:28] = JUMP_ADDRS;
  //   PC_UPPER4[3:0] = JUMP_ADDRS; ULAOP00 = ULAOP[0]; ULAOP01 = ULAOP[1]; ULAOP10 = ULAOP[2]

  // Notes on the sheet:
  //   Processador MIPS
  //   Ciência da Computação - 2024.2
  //   Arquitetura e Organização de Computadores
endmodule

module banco_registradores (
  input  [4:0] R1_num,
  input  [4:0] R2_num,
  input  [4:0] RW,
  input  [31:0] Din,
  input  WE,
  input  clk,
  output [31:0] R1,
  output [31:0] a0,
  output [31:0] R2,
  output [31:0] v0
);

  wire demultiplexer_1_out0, demultiplexer_1_out1, demultiplexer_1_out2, demultiplexer_1_out3,
       demultiplexer_2_out0, demultiplexer_2_out1, demultiplexer_2_out2, demultiplexer_2_out3,
       demultiplexer_2_out4, demultiplexer_2_out5, demultiplexer_2_out6, demultiplexer_2_out7,
       demultiplexer_3_out0, demultiplexer_3_out1, demultiplexer_3_out2, demultiplexer_3_out3,
       demultiplexer_3_out4, demultiplexer_3_out5, demultiplexer_3_out6, demultiplexer_3_out7,
       demultiplexer_4_out0, demultiplexer_4_out1, demultiplexer_4_out2, demultiplexer_4_out3,
       demultiplexer_4_out4, demultiplexer_4_out5, demultiplexer_4_out6, demultiplexer_4_out7,
       demultiplexer_5_out0, demultiplexer_5_out1, demultiplexer_5_out2, demultiplexer_5_out3,
       demultiplexer_5_out4, demultiplexer_5_out5, demultiplexer_5_out6, demultiplexer_5_out7;
  wire [31:0] _0__Zero_q, _1__at_q, _3__v1_q, _5__a1_q, _6__a2_q, _7__a3_q, _8__t0_q, _9__t1_q, _10__t2_q,
       _11__t3_q, _12__t4_q, _13__t5_q, _14__t6_q, _15__t7_q, _19__s3_q, _20__s4_q, _21__s5_q, _22__s6_q,
       _23__s7_q, _24__t8_q, _25__t9_q, _26__k0_q, _27__k1_q, _28__gp_q, _29__sp_q, _30__fp_q, ra, s0, s1, s2;

  Demultiplexer #(.select(2), .disabled(0)) demultiplexer_1 (
    .out0(demultiplexer_1_out0), .out1(demultiplexer_1_out1), .out2(demultiplexer_1_out2),
    .out3(demultiplexer_1_out3), .in(1'b1), .sel(RW[4:3]), .en(WE));
  Demultiplexer #(.select(3), .disabled(0)) demultiplexer_2 (
    .out0(demultiplexer_2_out0), .out1(demultiplexer_2_out1), .out2(demultiplexer_2_out2),
    .out3(demultiplexer_2_out3), .out4(demultiplexer_2_out4), .out5(demultiplexer_2_out5),
    .out6(demultiplexer_2_out6), .out7(demultiplexer_2_out7), .in(1'b1), .sel(RW[2:0]),
    .en(demultiplexer_1_out0));
  Demultiplexer #(.select(3), .disabled(0)) demultiplexer_3 (
    .out0(demultiplexer_3_out0), .out1(demultiplexer_3_out1), .out2(demultiplexer_3_out2),
    .out3(demultiplexer_3_out3), .out4(demultiplexer_3_out4), .out5(demultiplexer_3_out5),
    .out6(demultiplexer_3_out6), .out7(demultiplexer_3_out7), .in(1'b1), .sel(RW[2:0]),
    .en(demultiplexer_1_out1));
  Demultiplexer #(.select(3), .disabled(0)) demultiplexer_4 (
    .out0(demultiplexer_4_out0), .out1(demultiplexer_4_out1), .out2(demultiplexer_4_out2),
    .out3(demultiplexer_4_out3), .out4(demultiplexer_4_out4), .out5(demultiplexer_4_out5),
    .out6(demultiplexer_4_out6), .out7(demultiplexer_4_out7), .in(1'b1), .sel(RW[2:0]),
    .en(demultiplexer_1_out2));
  Demultiplexer #(.select(3), .disabled(0)) demultiplexer_5 (
    .out0(demultiplexer_5_out0), .out1(demultiplexer_5_out1), .out2(demultiplexer_5_out2),
    .out3(demultiplexer_5_out3), .out4(demultiplexer_5_out4), .out5(demultiplexer_5_out5),
    .out6(demultiplexer_5_out6), .out7(demultiplexer_5_out7), .in(1'b1), .sel(RW[2:0]),
    .en(demultiplexer_1_out3));
  Register #(.width(32)) _0__Zero (.D(Din), .en(demultiplexer_2_out0), .Q(_0__Zero_q));  // open: clk, clr
  Register #(.width(32)) _8__t0 (.D(Din), .en(demultiplexer_3_out0), .Q(_8__t0_q), .clk(clk));  // open: clr
  Register #(.width(32)) _16__s0 (.D(Din), .en(demultiplexer_4_out0), .Q(s0), .clk(clk));  // open: clr
  Register #(.width(32)) _24__t8 (.D(Din), .en(demultiplexer_5_out0), .Q(_24__t8_q), .clk(clk));  // open: clr
  Register #(.width(32)) _1__at (.D(Din), .en(demultiplexer_2_out1), .Q(_1__at_q), .clk(clk));  // open: clr
  Register #(.width(32)) _9__t1 (.D(Din), .en(demultiplexer_3_out1), .Q(_9__t1_q), .clk(clk));  // open: clr
  Register #(.width(32)) _17__s1 (.D(Din), .en(demultiplexer_4_out1), .Q(s1), .clk(clk));  // open: clr
  Register #(.width(32)) _25__t9 (.D(Din), .en(demultiplexer_5_out1), .Q(_25__t9_q), .clk(clk));  // open: clr
  Register #(.width(32)) _2__v0 (.D(Din), .en(demultiplexer_2_out2), .Q(v0), .clk(clk));  // open: clr
  Register #(.width(32)) _10__t2 (.D(Din), .en(demultiplexer_3_out2), .Q(_10__t2_q), .clk(clk));  // open: clr
  Register #(.width(32)) _18__s2 (.D(Din), .en(demultiplexer_4_out2), .Q(s2), .clk(clk));  // open: clr
  Register #(.width(32)) _26__k0 (.D(Din), .en(demultiplexer_5_out2), .Q(_26__k0_q), .clk(clk));  // open: clr
  Register #(.width(32)) _3__v1 (.D(Din), .en(demultiplexer_2_out3), .Q(_3__v1_q), .clk(clk));  // open: clr
  Register #(.width(32)) _11__t3 (.D(Din), .en(demultiplexer_3_out3), .Q(_11__t3_q), .clk(clk));  // open: clr
  Register #(.width(32)) _19__s3 (.D(Din), .en(demultiplexer_4_out3), .Q(_19__s3_q), .clk(clk));  // open: clr
  Register #(.width(32)) _27__k1 (.D(Din), .en(demultiplexer_5_out3), .Q(_27__k1_q), .clk(clk));  // open: clr
  Register #(.width(32)) _4__a0 (.D(Din), .en(demultiplexer_2_out4), .Q(a0), .clk(clk));  // open: clr
  Register #(.width(32)) _12__t4 (.D(Din), .en(demultiplexer_3_out4), .Q(_12__t4_q), .clk(clk));  // open: clr
  Register #(.width(32)) _20__s4 (.D(Din), .en(demultiplexer_4_out4), .Q(_20__s4_q), .clk(clk));  // open: clr
  Register #(.width(32)) _28__gp (.D(Din), .en(demultiplexer_5_out4), .Q(_28__gp_q), .clk(clk));  // open: clr
  Register #(.width(32)) _5__a1 (.D(Din), .en(demultiplexer_2_out5), .Q(_5__a1_q), .clk(clk));  // open: clr
  Register #(.width(32)) _13__t5 (.D(Din), .en(demultiplexer_3_out5), .Q(_13__t5_q), .clk(clk));  // open: clr
  Register #(.width(32)) _21__s5 (.D(Din), .en(demultiplexer_4_out5), .Q(_21__s5_q), .clk(clk));  // open: clr
  Register #(.width(32)) _29__sp (.D(Din), .en(demultiplexer_5_out5), .Q(_29__sp_q), .clk(clk));  // open: clr
  Register #(.width(32)) _6__a2 (.D(Din), .en(demultiplexer_2_out6), .Q(_6__a2_q), .clk(clk));  // open: clr
  Register #(.width(32)) _14__t6 (.D(Din), .en(demultiplexer_3_out6), .Q(_14__t6_q), .clk(clk));  // open: clr
  Register #(.width(32)) _22__s6 (.D(Din), .en(demultiplexer_4_out6), .Q(_22__s6_q), .clk(clk));  // open: clr
  Register #(.width(32)) _30__fp (.D(Din), .en(demultiplexer_5_out6), .Q(_30__fp_q), .clk(clk));  // open: clr
  Register #(.width(32)) _7__a3 (.D(Din), .en(demultiplexer_2_out7), .Q(_7__a3_q), .clk(clk));  // open: clr
  Register #(.width(32)) _15__t7 (.D(Din), .en(demultiplexer_3_out7), .Q(_15__t7_q), .clk(clk));  // open: clr
  Register #(.width(32)) _23__s7 (.D(Din), .en(demultiplexer_4_out7), .Q(_23__s7_q), .clk(clk));  // open: clr
  Register #(.width(32)) _31__ra (.D(Din), .en(demultiplexer_5_out7), .Q(ra), .clk(clk));  // open: clr
  Multiplexer #(.select(5), .width(32), .enable("false")) multiplexer_1 (
    .in0(_0__Zero_q), .in1(_1__at_q), .in2(v0), .in3(_3__v1_q), .in4(a0), .in5(_5__a1_q), .in6(_6__a2_q),
    .in7(_7__a3_q), .in8(_8__t0_q), .in9(_9__t1_q), .in10(_10__t2_q), .in11(_11__t3_q), .in12(_12__t4_q),
    .in13(_13__t5_q), .in14(_14__t6_q), .in15(_15__t7_q), .in16(s0), .in17(s1), .in18(s2), .in19(_19__s3_q),
    .in20(_20__s4_q), .in21(_21__s5_q), .in22(_22__s6_q), .in23(_23__s7_q), .in24(_24__t8_q),
    .in25(_25__t9_q), .in26(_26__k0_q), .in27(_27__k1_q), .in28(_28__gp_q), .in29(_29__sp_q),
    .in30(_30__fp_q), .in31(ra), .out(R1), .sel(R1_num));
  Multiplexer #(.select(5), .width(32), .enable("false")) multiplexer_2 (
    .in0(_0__Zero_q), .in1(_1__at_q), .in2(v0), .in3(_3__v1_q), .in4(a0), .in5(_5__a1_q), .in6(_6__a2_q),
    .in7(_7__a3_q), .in8(_8__t0_q), .in9(_9__t1_q), .in10(_10__t2_q), .in11(_11__t3_q), .in12(_12__t4_q),
    .in13(_13__t5_q), .in14(_14__t6_q), .in15(_15__t7_q), .in16(s0), .in17(s1), .in18(s2), .in19(_19__s3_q),
    .in20(_20__s4_q), .in21(_21__s5_q), .in22(_22__s6_q), .in23(_23__s7_q), .in24(_24__t8_q),
    .in25(_25__t9_q), .in26(_26__k0_q), .in27(_27__k1_q), .in28(_28__gp_q), .in29(_29__sp_q),
    .in30(_30__fp_q), .in31(ra), .out(R2), .sel(R2_num));

  // Other names for the same wires on the sheet: reg1[31:0] = R1; reg1_num[4:0] = R1_num; reg2[31:0] = R2;
  //   reg2_num[4:0] = R2_num; write_data[31:0] = Din; write_reg_num[4:0] = RW

  // Notes on the sheet:
  //   Input
  //   Output
endmodule

module ULA (
  input  [31:0] A,
  input  [31:0] B,
  input  [5:0] OP,
  output [31:0] Resultado,
  output igual
);

  wire comparator_1_lt;
  wire [31:0] adder_1_out, and_1_out, bit_extender_1_out, divider_1_out, multiplier_1_out, or_1_out,
       subtractor_1_out;

  Adder #(.width(32)) adder_1 (.a(A), .b(B), .out(adder_1_out));  // open: cin, cout
  Subtractor #(.width(32)) subtractor_1 (.a(A), .b(B), .out(subtractor_1_out));  // open: bin, bout
  Multiplier #(.width(32)) multiplier_1 (.a(A), .b(B), .out(multiplier_1_out));  // open: cin, cout
  Divider #(.width(32)) divider_1 (.a(A), .b(B), .out(divider_1_out));  // open: upper, rem
  Comparator #(.width(32)) comparator_1 (.a(A), .b(B), .eq(igual), .lt(comparator_1_lt));  // open: gt
  assign and_1_out = A & B;  // AND_Gate and_1, 32 bits wide
  assign or_1_out = A | B;  // OR_Gate or_1, 32 bits wide
  assign bit_extender_1_out = {{31{1'b0}}, comparator_1_lt};  // Bit_Extender bit_extender_1
  Multiplexer #(.select(3), .width(32), .enable("false")) multiplexer_1 (
    .in0(adder_1_out), .in1(subtractor_1_out), .in2(multiplier_1_out), .in3(divider_1_out), .in4(and_1_out),
    .in5(or_1_out), .in6(bit_extender_1_out), .out(Resultado), .sel(OP[2:0]));  // open: in7
endmodule

module UC (
  input  UC5,
  input  UC4,
  input  UC3,
  input  UC2,
  input  UC1,
  input  UC0,
  output WR,
  output BEQ,
  output BNE,
  output ULASRC,
  output REGDEST,
  output JUMP,
  output ULAOP02,
  output ULAOP01,
  output ULAOP00,
  output ULAOPSRC,
  output MUX_DIN,
  output MEM_WR
);

  wire and_1_out, and_2_out, and_3_out, and_4_out, and_7_out, and_8_out, and_9_out, and_10_out, and_11_out,
       and_12_out, and_15_out, and_16_out, and_17_out, and_18_out, and_19_out, and_20_out, and_21_out,
       and_22_out, and_23_out, and_24_out, and_25_out, and_26_out, and_27_out, and_28_out, and_29_out,
       not_1_out, not_2_out, not_3_out, not_4_out, not_5_out, not_6_out, not_7_out, not_8_out, not_9_out,
       not_10_out, not_11_out, not_12_out, not_13_out, not_14_out, not_15_out, not_16_out, not_17_out,
       not_18_out, not_19_out, not_20_out, not_21_out, not_22_out, not_23_out, not_24_out, not_25_out,
       not_26_out, not_27_out, not_28_out, not_29_out, not_30_out, not_31_out, not_32_out, not_33_out,
       not_34_out, not_35_out, not_36_out, not_37_out, not_38_out, not_39_out, not_40_out, not_41_out,
       not_42_out, not_43_out, not_44_out, not_45_out, not_46_out, not_47_out, not_48_out, not_49_out,
       not_50_out, not_51_out, not_52_out, not_53_out, not_54_out, not_55_out, not_56_out;

  not not_1 (not_1_out, UC5);
  not not_2 (not_2_out, UC4);
  not not_3 (not_3_out, UC3);
  not not_4 (not_4_out, UC2);
  not not_5 (not_5_out, UC5);
  not not_6 (not_6_out, UC4);
  not not_7 (not_7_out, UC3);
  not not_8 (not_8_out, UC1);
  not not_9 (not_9_out, UC0);
  not not_10 (not_10_out, UC5);
  not not_11 (not_11_out, UC4);
  not not_12 (not_12_out, UC2);
  not not_13 (not_13_out, UC0);
  not not_14 (not_14_out, UC5);
  not not_15 (not_15_out, UC4);
  not not_16 (not_16_out, UC3);
  not not_17 (not_17_out, UC5);
  not not_18 (not_18_out, UC4);
  not not_19 (not_19_out, UC3);
  not not_20 (not_20_out, UC1);
  not not_21 (not_21_out, UC5);
  not not_22 (not_22_out, UC4);
  not not_23 (not_23_out, UC2);
  not not_24 (not_24_out, UC1);
  not not_25 (not_25_out, UC3);
  not not_26 (not_26_out, UC2);
  not not_27 (not_27_out, UC0);
  not not_28 (not_28_out, UC5);
  not not_29 (not_29_out, UC4);
  not not_30 (not_30_out, UC0);
  or or_1 (REGDEST, UC0, UC1, UC2, UC3, UC4, UC5);
  not not_31 (not_31_out, UC5);
  not not_32 (not_32_out, UC4);
  not not_33 (not_33_out, UC3);
  not not_34 (not_34_out, UC0);
  not not_35 (not_35_out, UC5);
  not not_36 (not_36_out, UC4);
  not not_37 (not_37_out, UC2);
  not not_38 (not_38_out, UC0);
  not not_39 (not_39_out, UC2);
  not not_40 (not_40_out, UC1);
  not not_41 (not_41_out, UC5);
  not not_42 (not_42_out, UC4);
  not not_43 (not_43_out, UC2);
  not not_44 (not_44_out, UC3);
  not not_45 (not_45_out, UC0);
  not not_46 (not_46_out, UC1);
  not not_47 (not_47_out, UC0);
  not not_48 (not_48_out, UC0);
  not not_49 (not_49_out, UC0);
  or or_2 (ULAOPSRC, UC0, UC1, UC2, UC3);
  not not_50 (not_50_out, UC5);
  not not_51 (not_51_out, UC4);
  not not_52 (not_52_out, UC2);
  not not_53 (not_53_out, UC1);
  not not_54 (not_54_out, UC0);
  not not_55 (not_55_out, UC1);
  not not_56 (not_56_out, UC0);
  and and_1 (and_1_out, not_1_out, not_2_out, not_3_out, not_4_out);
  and and_2 (and_2_out, not_5_out, not_6_out, not_7_out, not_8_out, not_9_out);
  and and_3 (and_3_out, not_10_out, not_11_out, not_12_out, UC1, not_13_out);
  and and_4 (and_4_out, not_14_out, not_15_out, not_16_out, UC1, UC0);
  and and_5 (BEQ, not_17_out, not_18_out, not_19_out, UC2, not_20_out, UC0);
  and and_6 (BNE, not_21_out, not_22_out, UC3, not_23_out, not_24_out, UC0);
  and and_7 (and_7_out, not_25_out, not_26_out, UC0);
  and and_8 (and_8_out, UC2, not_27_out);
  and and_9 (and_9_out, not_28_out, not_29_out, UC3, not_30_out);
  and and_10 (and_10_out, UC3, UC2);
  and and_11 (and_11_out, UC4, UC0);
  and and_12 (and_12_out, UC5, UC0);
  and and_13 (JUMP, not_31_out, not_32_out, not_33_out, UC2, UC1, not_34_out);
  and and_14 (ULAOP02, not_35_out, not_36_out, UC3, not_37_out, UC1, not_38_out);
  and and_15 (and_15_out, not_39_out, UC1, UC0);
  and and_16 (and_16_out, UC2, not_40_out);
  and and_17 (and_17_out, not_41_out, not_42_out, UC3, not_43_out, UC1);
  and and_18 (and_18_out, not_44_out, UC1, not_45_out);
  and and_19 (and_19_out, UC2, not_46_out);
  and and_20 (and_20_out, UC2, not_47_out);
  and and_21 (and_21_out, UC4, UC1, not_48_out);
  and and_22 (and_22_out, UC5, UC1, not_49_out);
  and and_23 (and_23_out, UC2, UC1);
  and and_24 (and_24_out, not_50_out, not_51_out, UC3, not_52_out, not_53_out, not_54_out);
  and and_25 (and_25_out, UC3, not_55_out, not_56_out);
  and and_26 (and_26_out, UC3, UC1, UC0);
  and and_27 (and_27_out, UC3, UC2);
  and and_28 (and_28_out, UC4, UC3);
  and and_29 (and_29_out, UC5, UC3);
  or or_3 (WR, and_1_out, and_2_out, and_3_out, and_4_out);
  or or_4 (ULASRC, and_7_out, UC1, and_8_out, and_9_out, and_10_out, and_11_out, and_12_out);
  or or_5 (ULAOP01, and_15_out, and_16_out, and_17_out);
  or or_6 (ULAOP00, and_18_out, and_19_out, and_20_out, and_21_out, and_22_out);
  or or_7 (MUX_DIN, and_23_out, and_24_out);
  or or_8 (MEM_WR, and_25_out, and_26_out, and_27_out, and_28_out, and_29_out);
endmodule
